# Fritzing sketch djoeslightmeter (saved by Fritzing 1.0.4)
breadboards: 1
perfboards: 1

parts:
  A1 = Esp32-c3 super mini
  M1 = lcd color display 0.96in 80x160 8pin interface [package=THT]
  Composant1 = BH1750
  TP1 = TP4056 [chip_label=TP4056 package="DIP (Dual Inline) [THT]"]
  U1 = LIPO-1000mAh [package=lipo-1000]
  J1 = female pin header, 8 pins [form="♀ (female)"]
  J2 = female pin header, 5 pins [form="♀ (female)"]
  A2 = Esp32-c3 super mini

nets:
  N1: A1.Pin_2, J1.pin5
  N2: A1.Pin_3, J1.pin2
  N3: A1.Pin_4, J1.pin3
  N4: A1.Pin_6, J1.pin4
  N5: A1.Pin_9, J2.pin3
  N6: A1.Pin_10, J2.pin4
  N7: A1.Pin_13, J1.pin6
  N8: A1.Pin_14, J1.pin7, J2.pin5
  N9: A1.Pin_15, J1.pin8, J2.pin1, J2.pin2
  GND: M1.GND, Composant1.GND, Composant1.ADDR, TP1.pin6, A2.Pin_15
  VCC: M1.VCC, Composant1.VCC, TP1.pin3, A2.Pin_14
  N10: M1.SCL, A2.Pin_13
  N11: M1.SDA, A2.Pin_2
  N12: M1.RES, A2.Pin_6
  N13: M1.DC, A2.Pin_4
  N14: M1.CS, A2.Pin_3
  N15: Composant1.SCL, A2.Pin_9
  N16: Composant1.SDA, A2.Pin_10
  N17: TP1.pin4, U1.+
  N18: TP1.pin5, U1.-

custom parts:
  Esp32-c3 super mini: ESP32-C3 Development Board ESP32 SuperMini Development Board ESP32 Development Board WiFi Bluetooth.
  lcd color display 0.96in 80x160 8pin interface: Ips 0.96 Inch 8 Pin Spi Hd 65K Full Color Tft Module St7735 Drive Ic 80 x 160 Lcd Display 3.3V Spi Interface.
  BH1750: Light Sensor
  TP4056: A DIP stand-in part for whatever IC you want. With 6 pins on a 300mil dual inline package (DIP) footprint.
